# Fritzing sketch esquemaeletrico (saved by Fritzing 0.9.10b)

parts:
  SEN1 = Pulse Sensor [package=SIP-3]
  U1 = LuaNode32 / ESP32 [part_number=ESP32S-PIN30]
  U2 = LIPO-1000mAh [package=lipo-1000]
  LED1 = LEDs [package=led10mm]
  R1 = Resistor [tolerance=±5% resistance=220 package="0402 [SMD]"]
  S1 = Taiway 100-SP-X-T1 SPDT Miniature Toggle Switch [part_number=100-SP-X-T1-0-0-B1-M1 package=THT]  # not connected

nets:
  GND: SEN1.GND, U1.GND, U2.-, LED1.C
  VCC: SEN1.VCC, U1.3V3
  N1: SEN1.Signal, U1.D4
  N2: U1.Vin, U2.+
  N3: U1.D19, R1.Pin_0

custom parts:
  Pulse Sensor: Pulse Sensor Optical Heart Beat Sensor
  LuaNode32 / ESP32: New Image for LuaNode32 DOIT ESP32 DEVKIT V1. Base parts from LuaNode32 / ESP32 ESP32 based LuaNode32 by G.Noorlander DOIT Esp32 DevKit v1 (30 pins long, 11 pins width) by Werner Rothschopf (modified by vanepp Dec 2018)
